// Logisim project questao3.circ as structural Verilog: 1 circuit, main circuit main
module main (
  input  Clock,
  input  Input,
  output out_3,
  output out_4
);

  questao1_main Mealy (.Clock(Clock), .Input(Input), .out_3(out_3));
  questao2_main Moore (.Clock(Clock), .Input(Input), .out_3(out_4));
endmodule
